# Fritzing sketch SLEDGE_Prototype_V1 (saved by Fritzing 0.9.3b)
breadboards: 2

parts:
  Part1 = Logic Level Converter  # not connected
  Part2 = I2C level shifter bidirectional  # not connected
  Part3 = Audio Jack Breakout  # not connected
  C2 = Electrolytic Capacitor [capacitance=1000µF voltage=5V package="300 mil [THT, electrolytic]"]
  C3 = Electrolytic Capacitor [capacitance=100µF package="200 mil [THT, electrolytic]"]  # not connected
  R1 = Resistor [tolerance=±5% resistance=10k package="0603 [SMD]"]  # not connected
  R2 = Resistor [tolerance=±5% resistance=10k package="0603 [SMD]"]  # not connected
  R3 = Resistor [tolerance=±5% resistance=100k package="0603 [SMD]"]  # not connected
  RGB_SMD_LED1 = SMD RGB LED (WS2812) [package=5050]
  RGB_SMD_LED2 = SMD RGB LED (WS2812) [package=5050]  # not connected
  RGB_SMD_LED3 = SMD RGB LED (WS2812) [package=5050]  # not connected
  RGB_SMD_LED4 = SMD RGB LED (WS2812) [package=5050]  # not connected
  RGB_SMD_LED5 = SMD RGB LED (WS2812) [package=5050]  # not connected
  RGB_SMD_LED6 = SMD RGB LED (WS2812) [package=5050]  # not connected
  RGB_SMD_LED7 = SMD RGB LED (WS2812) [package=5050]  # not connected
  R4 = Resistor [tolerance=±5% resistance=100k package="0603 [SMD]"]  # not connected
  RGB_SMD_LED8 = SMD RGB LED (WS2812B) [package=5050]  # not connected
  RGB_SMD_LED9 = SMD RGB LED (WS2812B) [package=5050]  # not connected
  RGB_SMD_LED10 = SMD RGB LED (WS2812B) [package=5050]  # not connected
  RGB_SMD_LED11 = SMD RGB LED (WS2812B) [package=5050]  # not connected
  RGB_SMD_LED12 = SMD RGB LED (WS2812B) [package=5050]  # not connected
  RGB_SMD_LED13 = SMD RGB LED (WS2812B) [package=5050]  # not connected
  RGB_SMD_LED14 = SMD RGB LED (WS2812B) [package=5050]  # not connected
  J1 = Power Jack [package=power_jack_pth]  # not connected
  VCC1 = 4 x AAA Battery Mount  # not connected
  R5 = Resistor [tolerance=±5% resistance=220 package="0603 [SMD]"]
  R6 = Resistor [tolerance=±5% resistance=470 package="0603 [SMD]"]  # not connected
  R7 = Resistor [tolerance=±5% resistance=330 package="0603 [SMD]"]  # not connected
  R8 = Resistor [tolerance=±5% resistance=470 package="0603 [SMD]"]  # not connected
  R9 = Resistor [tolerance=±5% resistance=330 package="0603 [SMD]"]  # not connected
  R10 = Resistor [tolerance=±5% resistance=470 package="0603 [SMD]"]  # not connected
  M1 = DOIT Esp32 DevKit v1 (30 pins long, 11 pins width) [part_number=ESP32S-PIN30]
  SN74HCT245N = IC, DIP package, 20 pins [chip_label=SN74HCT245N]

nets:
  N1: C2.-, RGB_SMD_LED1.DOut
  N2: C2.+, RGB_SMD_LED1.VCC
  N3: RGB_SMD_LED1.DIn, R5.Pin_0
  N4: M1.GND, SN74HCT245N.pin19
  N5: M1.D27, SN74HCT245N.pin18
  N6: M1.VIN, SN74HCT245N.pin20

notes:
  1x ESP32 Microcontroller
  1x 3.3V to 5V logic level shifter
  1x 3.5Mm Stereo Audio Jack Breakout Board
  1x 3.5Mm Audio Jack Cable
  1x 1000uf Capacitor [DOESNT HAVE?]
  1x 100uf DC blocking Capacitor for Audio Input Signal
  2x 10k Resistors for converting stereo audio signal to mono
  2x 100k Resistors for adding DC bias to analog audio input signal
  1x Strip of Addressable LEDs
  1x 5V DC Power Supply
  1x 300-400 ohm Resistor per led Strip Data Line

custom parts:
  SMD RGB LED (WS2812B): The WS2812B is an RGB LED with a WS2811 control IC built right into the LED. Its improvement over its WS2812 ancestor is the reduction to 4 pins (a single power supply instead of 2) and dropping the requirement for the external resistors. The manufacturer says it has a better reverse connect protection.
  DOIT Esp32 DevKit v1 (30 pins long, 11 pins width): The DOIT Esp32 DevKit v1 is one of the development board created by DOIT to evaluate the ESP-WROOM-32 module. It is based on the ESP32 microcontroller that boasts Wifi, Bluetooth, Ethernet and Low Power support all in a single chip. (vanepp) made breadboard work, adjusted pin numbering and labels and reduced size of schematic and cleaned up pcb. This chip is 30pins long (2 x15) and 11 pins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
